// Logisim project cpu.circ as structural Verilog: 1 circuit, main circuit main
module main (
  input  [31:0] INSTRUCTION,
  input  in_2,
  output [31:0] PROGRAM_COUNTER,
  output [31:0] ra,
  output [31:0] sp,
  output [31:0] t0,
  output [31:0] t1,
  output [31:0] t2,
  output [31:0] s0,
  output [31:0] s1,
  output [31:0] a0
);

  wire BSel_1, comparator_1_eq, comparator_2_gt, comparator_3_eq, comparator_4_gt, data_hazard1,
       data_hazard2, DMEM_p1, RegWEn_1;
  wire [2:0] ImmSel_1;
  wire [3:0] Sel;
  wire [4:0] Addrd_1, Addrs1_1, Addrs2_1;
  wire [31:0] adder_1_out, ALUres_1, imm_1, INSTRUCTION_1, multiplexer_1_out, multiplexer_2_out,
       multiplexer_3_out, PROGRAM_COUNTER_1, rs1, rs1_1, rs2, rs2_1;

  control_logic control_logic_1 (
    .BSel(BSel_1), .ImmSel(ImmSel_1), .RegWEn(RegWEn_1),
    .inst({INSTRUCTION_1[31:25], Addrs2_1, Addrs1_1, INSTRUCTION_1[14:12], Addrd_1, INSTRUCTION_1[6:0]}));  // open: ASel, BrUn, PCSel, BrLt, BrEq, ALUSel, MemRW, WBSel
  Adder #(.width(32)) adder_1 (.a(PROGRAM_COUNTER), .b(32'h4), .out(adder_1_out));  // open: cin, cout
  Register #(.width(32)) register_1 (.D(PROGRAM_COUNTER), .clk(in_2), .Q(PROGRAM_COUNTER_1));  // open: en, clr
  Register #(.width(32)) register_2 (
    .D(INSTRUCTION), .clk(in_2),
    .Q({INSTRUCTION_1[31:25], Addrs2_1, Addrs1_1, INSTRUCTION_1[14:12], Addrd_1, INSTRUCTION_1[6:0]}));  // open: en, clr
  Register #(.width(32)) PC (.D(adder_1_out), .clk(in_2), .Q(PROGRAM_COUNTER));  // open: en, clr
  imm_gen imm_gen_1 (
    .ImmSel(ImmSel_1),
    .inst({INSTRUCTION_1[31:25], Addrs2_1, Addrs1_1, INSTRUCTION_1[14:12], Addrd_1, INSTRUCTION_1[6:0]}),
    .imm(imm_1));
  Register #(.width(32)) register_3 (.D(multiplexer_1_out), .clk(in_2), .Q(rs1_1));  // open: en, clr
  Multiplexer #(.width(32), .enable("false")) multiplexer_1 (
    .in0(rs1), .in1(ALUres_1), .out(multiplexer_1_out), .sel(data_hazard1));
  Register #(.width(32)) register_4 (.D(multiplexer_2_out), .clk(in_2), .Q(rs2_1));  // open: en, clr
  Multiplexer #(.width(32), .enable("false")) multiplexer_2 (
    .in0(rs2), .in1(ALUres_1), .out(multiplexer_2_out), .sel(data_hazard1));
  regfile_main RegFile (
    .rs2(INSTRUCTION[24:20]), .rd(Addrd_1), .Read_Data_1(rs1), .Read_Data_2(rs2), .ra(ra), .sp(sp), .t0(t0),
    .t1(t1), .t2(t2), .s0(s0), .s1(s1), .a0(a0), .rs1(INSTRUCTION[19:15]), .Write_Data(ALUres_1),
    .RegWEn(RegWEn_1), .clk(in_2));
  // branch_comp branch_comp_1: pin names not known
  Comparator #(.width(5), .mode("unsigned")) comparator_1 (
    .a(Addrd_1), .b(INSTRUCTION[19:15]), .eq(comparator_1_eq));  // open: gt, lt
  Comparator #(.width(5), .mode("unsigned")) comparator_2 (
    .a(Addrd_1), .b({5{1'b0}}), .gt(comparator_2_gt));  // open: eq, lt
  Comparator #(.width(5), .mode("unsigned")) comparator_3 (
    .a(Addrd_1), .b(INSTRUCTION[24:20]), .eq(comparator_3_eq));  // open: gt, lt
  Comparator #(.width(5), .mode("unsigned")) comparator_4 (
    .a(Addrd_1), .b({5{1'b0}}), .gt(comparator_4_gt));  // open: eq, lt
  and and_1 (data_hazard1, comparator_1_eq, comparator_2_gt);
  and and_2 (data_hazard2, comparator_3_eq, comparator_4_gt);
  Multiplexer #(.width(32), .enable("false")) multiplexer_3 (
    .in0(rs2_1), .in1(imm_1), .out(multiplexer_3_out), .sel(BSel_1));
  alu Arithmetic_Logic_Unit (.ALUSel(Sel), .Result(ALUres_1), .A(rs1_1), .B(multiplexer_3_out));
  // mem_main DMEM: pin names not known; wires that end beside it: DMEM_p1

  // Other names for the same wires on the sheet: clk = in_2; Addrd[4:0] = INSTRUCTION[11:7];
  //   Addrs1[4:0] = INSTRUCTION[19:15]; Addrs2[4:0] = INSTRUCTION[24:20];
  //   INSTRUCTION_1 (some bits) = {Addrs2_1, Addrs1_1, Addrd_1}

  // Notes on the sheet:
  //   Output
  //   IMEM (do **NOT** move this)
  //   Inputs
  //   It is OK to move the PC, RegFile, ALU, MEM, Branch Comp, Imm Gen, and Control Logic to wherever is most convenient for you when constructing your CPU, and to delete this text
  //   Inputs/Outputs for testing. Do **NOT** move these.
endmodule
